# Fritzing sketch schematic design (saved by Fritzing 0.9.3b)
breadboards: 1

parts:
  R1 = Resistor [tolerance=±5% resistance=220 package=THT]
  Εξάρτημα1 = Arduino Uno (Rev3)
  R9 = Resistor [tolerance=±5% resistance=10k package=THT]
  LED6 = LED - 5mm [color="Red (660nm)" package="5 mm [THT]"]
  LED3 = LED - 5mm [color="Red (660nm)" package="5 mm [THT]"]
  Q3 = NPN-Transistor [package="TO92 [THT]"]
  R10 = Resistor [tolerance=±5% resistance=220 package=THT]
  R11 = Resistor [tolerance=±5% resistance=220 package=THT]
  R12 = Resistor [tolerance=±5% resistance=220 package=THT]
  LED7 = LED - 5mm [color="Orange (620nm)" package="5 mm [THT]"]
  LED8 = LED - 5mm [color="Orange (620nm)" package="5 mm [THT]"]
  R13 = Resistor [tolerance=±5% resistance=10k package=THT]
  Q4 = NPN-Transistor [package="TO92 [THT]"]
  R14 = Resistor [tolerance=±5% resistance=220 package=THT]
  R15 = Resistor [tolerance=±1% resistance=220 package=THT]
  LED9 = LED - 5mm [color="Green (560nm)" package="5 mm [THT]"]
  LED10 = LED - 5mm [color="Green (560nm)" package="5 mm [THT]"]
  R16 = Resistor [tolerance=±5% resistance=10k package=THT]
  Q5 = NPN-Transistor [package="TO92 [THT]"]
  M4 = Dagu DGServo 9g (Top view) [part_number=RS001B]
  R26 = Resistor [tolerance=±5% resistance=220 package=THT]
  R27 = Resistor [tolerance=±5% resistance=3.3k package=THT]
  R28 = Resistor [tolerance=±5% resistance=220 package=THT]
  R29 = Resistor [tolerance=±5% resistance=3.3k package=THT]
  LED22 = LED - 5mm [color="Infrared (940nm)" package="5 mm [THT]"]
  LED23 = LED - 5mm [color="Infrared (850nm)" package="5 mm [THT]"]
  LED24 = LED - 5mm [color="Infrared (850nm)" package="5 mm [THT]"]
  LED25 = LED - 5mm [color="Infrared (940nm)" package="5 mm [THT]"]
  M5 = Dagu DGServo 9g (Top view) [part_number=RS001B]

nets:
  N1: R1.Pin_0, LED3.cathode
  N2: R1.Pin_1, Q3.C, R10.Pin_1
  N3: Εξάρτημα1.A0, R29.Pin_1, LED22.cathode
  N4: Εξάρτημα1.A1, R27.Pin_1, LED25.cathode
  N5: Εξάρτημα1.D8, M4.pulse
  N6: Εξάρτημα1.D9_PWM, M5.pulse
  N7: Εξάρτημα1.D5_PWM, R9.Pin_0
  N8: Εξάρτημα1.D6_PWM, R13.Pin_0
  N9: Εξάρτημα1.D7, R16.Pin_0
  VCC: Εξάρτημα1.5V, LED6.anode, LED3.anode, LED7.anode, LED8.anode, LED9.anode, LED10.anode, M4.vcc, R27.Pin_0, R29.Pin_0, LED23.cathode, LED24.cathode, M5.vcc
  GND: Εξάρτημα1.GND, Q3.E, Q4.E, Q5.E, M4.gnd, R26.Pin_0, R28.Pin_0, LED22.anode, LED25.anode, M5.gnd
  N10: R9.Pin_1, Q3.B
  N11: LED6.cathode, R10.Pin_0
  N12: R11.Pin_0, LED8.cathode
  N13: R11.Pin_1, R12.Pin_1, Q4.C
  N14: R12.Pin_0, LED7.cathode
  N15: R13.Pin_1, Q4.B
  N16: R14.Pin_0, LED10.cathode
  N17: R14.Pin_1, R15.Pin_1, Q5.C
  N18: R15.Pin_0, LED9.cathode
  N19: R16.Pin_1, Q5.B
  N20: R26.Pin_1, LED23.anode
  N21: R28.Pin_1, LED24.anode

notes:
  ΣΥΝΔΕΣΜΟΛΟΓΙΑ ΕΞΥΠΝΗ ΔΙΑΒΑΣΗ ΖΩΩΝ
